# Fritzing sketch Wire_APDS (saved by Fritzing 1.0.6)
breadboards: 1

parts:
  Mod1 = Raspberry Pi Pico W
  R1 = Resistor [tolerance=±1% power=0.25W resistance=50 package=THT]
  R2 = Resistor [tolerance=±1% power=0.25W resistance=50 package=THT]
  R3 = Resistor [tolerance=±1% power=0.25W resistance=50 package=THT]
  LED1 = RGB LED (com. cathode, rgb) [color="Red (633nm)" current=0.030A package="5 mm [THT]"]
  Bauteil2 = Adafruit APDS-9960 [part_number="Adafruit #3595"]

nets:
  N1: Mod1.pin_3, Mod1.pin_8, Mod1.pin_13, Mod1.pin_18, Mod1.pin_23, Mod1.pin_28, Mod1.pin_33, Mod1.pin_38, LED1.common_cathode, Bauteil2.GND
  N2: Mod1.pin_19, Bauteil2.SDA
  N3: Mod1.pin_20, Bauteil2.SCL
  N4: Mod1.pin_24, R2.Pin_1
  N5: Mod1.pin_25, R3.Pin_1
  N6: Mod1.pin_26, R1.Pin_1
  N7: Mod1.pin_36, Bauteil2.3.3V
  N8: R1.Pin_0, LED1.blue_anode
  N9: R2.Pin_0, LED1.red_anode
  N10: R3.Pin_0, LED1.green_anode

notes:
  Note: The actual board may look
  slightly different, but has the same pins

custom parts:
  Raspberry Pi Pico W: Raspberry Pi Pico W. Based around the RP2040 microcontroller the Pico W is a low cost microcontroller device bringing Raspberry Pi quality, cost, and easy of use to the microcontroller space. The areas marked KEEPOUT in pcb silkscreen should not have traces running through them to avoid shorts on a soldered in module!
  Adafruit APDS-9960: The APDS9960 from Avago Technologies has an integrated IR LED and driver, along with four directional photodiodes that sense reflected IR energy from the LED. It's proximity detection feature allows it to measure the distance an object is from the front of the sensor (up to a few centimeters) with 8 bit resolution. Since there are four IR sensors, you can measure the changes in light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
